# Fritzing sketch Peripheral Project Circuit (saved by Fritzing 0.9.3b)
breadboards: 1

parts:
  Part1 = Arduino Uno (Rev3)
  LED1 = LED - 5mm [color="Red (633nm)" package="5 mm [THT]"]
  J1 = Piezo Speaker
  J2 = Piezo Speaker
  J3 = Basic Servo
  J4 = Basic Servo
  Grove1 = Grove Light Sensor
  Grove2 = Grove Light Sensor
  Grove3 = Grove Light Sensor
  Grove4 = Grove Light Sensor
  Grove5 = Grove Light Sensor
  Grove6 = Grove Light Sensor

nets:
  N1: Part1.A0, Grove3.SIG
  N2: Part1.A1, Grove6.SIG
  N3: Part1.A2, Grove2.SIG
  N4: Part1.A3, Grove1.SIG
  N5: Part1.A4/SDA, Grove5.SIG
  N6: Part1.A5/SCL, Grove4.SIG
  N7: Part1.D9_PWM, J3.pulse
  N8: Part1.D11_PWM/MOSI, J4.pulse
  GND: Part1.GND, LED1.cathode, J1.pin1, J3.gnd, J4.gnd, Grove1.GND, Grove2.GND, Grove3.GND, Grove4.GND, Grove5.GND, Grove6.GND
  N9: Part1.D6_PWM, J1.pin2, J2.pin2
  VCC: Part1.5V, LED1.anode, J3.vcc, Grove2.VCC, Grove3.VCC, Grove4.VCC
  VCC_2: J4.vcc, Grove1.VCC, Grove5.VCC, Grove6.VCC
